// Logisim project 8bit ALU simulation.circ.circ as structural Verilog: 20 circuits, main circuit full artim
module _1adder (
  input  A,
  input  B,
  input  in_3,
  output SUM,
  output C_OUT
);

  wire and_1_out, and_2_out, xor_1_out;

  xor xor_1 (xor_1_out, A, B);
  xor xor_2 (SUM, xor_1_out, in_3);
  and and_1 (and_1_out, in_3, xor_1_out);
  and and_2 (and_2_out, B, A);
  or or_1 (C_OUT, and_1_out, and_2_out);
endmodule

module _4bit_adder (
  input  C_IN,
  input  A0,
  input  B0,
  input  A1,
  input  B1,
  input  A2,
  input  B2,
  input  A3,
  input  B3,
  output S0,
  output S1,
  output S2,
  output S3,
  output C_OUT
);

  wire n1adder_1_c_out, n1adder_2_c_out, n1adder_3_c_out;

  _1adder u_1adder_1 (.A(A0), .B(B0), .in_3(C_IN), .SUM(S0), .C_OUT(n1adder_1_c_out));
  _1adder u_1adder_2 (.A(A1), .B(B1), .in_3(n1adder_1_c_out), .SUM(S1), .C_OUT(n1adder_2_c_out));
  _1adder u_1adder_3 (.A(A2), .B(B2), .in_3(n1adder_2_c_out), .SUM(S2), .C_OUT(n1adder_3_c_out));
  _1adder u_1adder_4 (.A(A3), .B(B3), .in_3(n1adder_3_c_out), .SUM(S3), .C_OUT(C_OUT));
endmodule

// FULL ADDER
module _8bit_adder (
  input  C_IN,
  input  A0,
  input  B0,
  input  A1,
  input  B1,
  input  A2,
  input  B2,
  input  A3,
  input  B3,
  input  A4,
  input  B4,
  input  A5,
  input  B5,
  input  A6,
  input  B6,
  input  A7,
  input  B7,
  output S0,
  output S1,
  output S2,
  output S3,
  output S4,
  output S5,
  output S6,
  output S7,
  output C_OUT
);

  wire n4bit_adder_1_c_out;

  _4bit_adder u_4bit_adder_1 (
    .C_IN(C_IN), .A0(A0), .B0(B0), .A1(A1), .B1(B1), .A2(A2), .B2(B2), .A3(A3), .B3(B3), .S0(S0), .S1(S1),
    .S2(S2), .S3(S3), .C_OUT(n4bit_adder_1_c_out));
  _4bit_adder u_4bit_adder_2 (
    .C_IN(n4bit_adder_1_c_out), .A0(A4), .B0(B4), .A1(A5), .B1(B5), .A2(A6), .B2(B6), .A3(A7), .B3(B7),
    .S0(S4), .S1(S5), .S2(S6), .S3(S7), .C_OUT(C_OUT));
endmodule

module adder_with_sub (
  input  CO,
  input  S1,
  input  S0,
  input  A0,
  input  B0,
  input  A1,
  input  B1,
  input  A2,
  input  B2,
  input  A3,
  input  B3,
  input  A4,
  input  B4,
  input  A5,
  input  B5,
  input  A6,
  input  B6,
  input  A7,
  input  B7,
  input  in_20,
  output S0_2,
  output S1_2,
  output S2,
  output S3,
  output S4,
  output S5,
  output S6,
  output S7,
  output C_OUT
);

  wire n4x1_mux_1_out_7, n4x1_mux_2_out_7, n4x1_mux_3_out_7, n4x1_mux_4_out_7, n4x1_mux_5_out_7,
       n4x1_mux_6_out_7, n4x1_mux_7_out_7, n4x1_mux_8_out_7, not_1_out, not_2_out, not_3_out, not_4_out,
       not_5_out, not_6_out, not_7_out, not_8_out, not_9_out;

  not not_1 (not_1_out, B0);
  not not_2 (not_2_out, B1);
  not not_3 (not_3_out, B2);
  not not_4 (not_4_out, B3);
  not not_5 (not_5_out, B4);
  not not_6 (not_6_out, B5);
  not not_7 (not_7_out, B6);
  not not_8 (not_8_out, B7);
  not not_9 (not_9_out, in_20);
  _4x1_mux u_4x1_mux_1 (
    .in_1(B0), .in_2(not_1_out), .in_3(in_20), .in_4(not_9_out), .in_5(S1), .in_6(S0),
    .out_7(n4x1_mux_1_out_7));
  _4x1_mux u_4x1_mux_2 (
    .in_1(B1), .in_2(not_2_out), .in_3(in_20), .in_4(not_9_out), .in_5(S1), .in_6(S0),
    .out_7(n4x1_mux_2_out_7));
  _4x1_mux u_4x1_mux_3 (
    .in_1(B2), .in_2(not_3_out), .in_3(in_20), .in_4(not_9_out), .in_5(S1), .in_6(S0),
    .out_7(n4x1_mux_3_out_7));
  _4x1_mux u_4x1_mux_4 (
    .in_1(B3), .in_2(not_4_out), .in_3(in_20), .in_4(not_9_out), .in_5(S1), .in_6(S0),
    .out_7(n4x1_mux_4_out_7));
  _4x1_mux u_4x1_mux_5 (
    .in_1(B4), .in_2(not_5_out), .in_3(in_20), .in_4(not_9_out), .in_5(S1), .in_6(S0),
    .out_7(n4x1_mux_5_out_7));
  _4x1_mux u_4x1_mux_6 (
    .in_1(B5), .in_2(not_6_out), .in_3(in_20), .in_4(not_9_out), .in_5(S1), .in_6(S0),
    .out_7(n4x1_mux_6_out_7));
  _4x1_mux u_4x1_mux_7 (
    .in_1(B6), .in_2(not_7_out), .in_3(in_20), .in_4(not_9_out), .in_5(S1), .in_6(S0),
    .out_7(n4x1_mux_7_out_7));
  _4x1_mux u_4x1_mux_8 (
    .in_1(B7), .in_2(not_8_out), .in_3(in_20), .in_4(not_9_out), .in_5(S1), .in_6(S0),
    .out_7(n4x1_mux_8_out_7));
  _8bit_adder u_8bit_adder_1 (
    .C_IN(CO), .A0(A0), .B0(n4x1_mux_1_out_7), .A1(A1), .B1(n4x1_mux_2_out_7), .A2(A2),
    .B2(n4x1_mux_3_out_7), .A3(A3), .B3(n4x1_mux_4_out_7), .A4(A4), .B4(n4x1_mux_5_out_7), .A5(A5),
    .B5(n4x1_mux_6_out_7), .A6(A6), .B6(n4x1_mux_7_out_7), .A7(A7), .B7(n4x1_mux_8_out_7), .S0(S0_2),
    .S1(S1_2), .S2(S2), .S3(S3), .S4(S4), .S5(S5), .S6(S6), .S7(S7), .C_OUT(C_OUT));
endmodule

module _4bit_buffer (
  input  E,
  input  A0,
  input  A1,
  input  A2,
  input  A3,
  output S0,
  output S1,
  output S2,
  output S3
);

  assign S0 = E ? A0 : 1'bz;  // Controlled_Buffer controlled_buffer_1
  assign S1 = E ? A1 : 1'bz;  // Controlled_Buffer controlled_buffer_2
  assign S2 = E ? A2 : 1'bz;  // Controlled_Buffer controlled_buffer_3
  assign S3 = E ? A3 : 1'bz;  // Controlled_Buffer controlled_buffer_4
endmodule

module _8bit_buffer (
  input  E,
  input  A0,
  input  A1,
  input  A2,
  input  A3,
  input  A4,
  input  A5,
  input  A6,
  input  A7,
  output S0,
  output S1,
  output S2,
  output S3,
  output S4,
  output S5,
  output S6,
  output S7
);

  assign S0 = E ? A0 : 1'bz;  // Controlled_Buffer controlled_buffer_1
  assign S1 = E ? A1 : 1'bz;  // Controlled_Buffer controlled_buffer_2
  assign S2 = E ? A2 : 1'bz;  // Controlled_Buffer controlled_buffer_3
  assign S3 = E ? A3 : 1'bz;  // Controlled_Buffer controlled_buffer_4
  assign S4 = E ? A4 : 1'bz;  // Controlled_Buffer controlled_buffer_5
  assign S5 = E ? A5 : 1'bz;  // Controlled_Buffer controlled_buffer_6
  assign S6 = E ? A6 : 1'bz;  // Controlled_Buffer controlled_buffer_7
  assign S7 = E ? A7 : 1'bz;  // Controlled_Buffer controlled_buffer_8
endmodule

module flip_flop (
  input  CLR,
  input  D,
  input  CLK,
  input  PRE,
  output Q,
  output NOT_Q
);

  wire nand_1_out, nand_2_out, nand_3_out, nand_4_out, not_1_out, not_2_out;

  not not_1 (not_1_out, CLR);
  not not_2 (not_2_out, PRE);
  nand nand_1 (nand_1_out, nand_4_out, not_2_out, nand_2_out);
  nand nand_2 (nand_2_out, nand_1_out, not_1_out, CLK);
  nand nand_3 (nand_3_out, nand_2_out, CLK, nand_4_out);
  nand nand_4 (nand_4_out, nand_3_out, not_1_out, D);
  nand nand_5 (Q, nand_2_out, not_2_out, NOT_Q);
  nand nand_6 (NOT_Q, Q, not_1_out, nand_3_out);
endmodule

module _1bit_reg (
  input  LOAD,
  input  CLR,
  input  CLK,
  input  A0,
  output Q,
  output NOT_Q
);

  wire and_1_out, and_2_out, not_1_out, or_1_out;

  not not_1 (not_1_out, LOAD);
  and and_1 (and_1_out, Q, not_1_out);
  and and_2 (and_2_out, LOAD, A0);
  flip_flop flip_flop_1 (.D(or_1_out), .CLK(CLK), .CLR(CLR), .Q(Q), .NOT_Q(NOT_Q));  // open: PRE
  or or_1 (or_1_out, and_1_out, and_2_out);
endmodule

module _4bit_reg (
  input  A0,
  input  A1,
  input  A2,
  input  A3,
  input  CLR,
  input  LOAD,
  input  CLK,
  output S0,
  output S1,
  output S2,
  output S3
);

  _1bit_reg u_1bit_reg_1 (.CLR(CLR), .A0(A0), .LOAD(LOAD), .CLK(CLK), .Q(S0));  // open: NOT_Q
  _1bit_reg u_1bit_reg_2 (.CLR(CLR), .A0(A1), .LOAD(LOAD), .CLK(CLK), .Q(S1));  // open: NOT_Q
  _1bit_reg u_1bit_reg_3 (.CLR(CLR), .A0(A2), .LOAD(LOAD), .CLK(CLK), .Q(S2));  // open: NOT_Q
  _1bit_reg u_1bit_reg_4 (.CLR(CLR), .A0(A3), .LOAD(LOAD), .CLK(CLK), .Q(S3));  // open: NOT_Q
endmodule

module _4bit_buffer_reg (
  input  A0,
  input  A1,
  input  A2,
  input  A3,
  input  CLR,
  input  LOAD,
  input  CLK,
  input  ENABLE,
  output S0,
  output S1,
  output S2,
  output S3
);

  wire n4bit_reg_1_s0, n4bit_reg_1_s1, n4bit_reg_1_s2, n4bit_reg_1_s3;

  _4bit_reg u_4bit_reg_1 (
    .A0(A0), .A1(A1), .A2(A2), .A3(A3), .CLR(CLR), .LOAD(LOAD), .CLK(CLK), .S0(n4bit_reg_1_s0),
    .S1(n4bit_reg_1_s1), .S2(n4bit_reg_1_s2), .S3(n4bit_reg_1_s3));
  _4bit_buffer u_4bit_buffer_1 (
    .A0(n4bit_reg_1_s0), .A1(n4bit_reg_1_s1), .A2(n4bit_reg_1_s2), .A3(n4bit_reg_1_s3), .E(ENABLE), .S0(S0),
    .S1(S1), .S2(S2), .S3(S3));
endmodule

module _8bit_reg (
  input  A0,
  input  A1,
  input  A2,
  input  A3,
  input  A4,
  input  A5,
  input  A6,
  input  A7,
  input  CLR,
  input  LOAD,
  input  CLK,
  output S0,
  output S1,
  output S2,
  output S3,
  output S4,
  output S5,
  output S6,
  output S7
);

  _1bit_reg u_1bit_reg_1 (.CLR(CLR), .A0(A0), .LOAD(LOAD), .CLK(CLK), .Q(S0));  // open: NOT_Q
  _1bit_reg u_1bit_reg_2 (.CLR(CLR), .A0(A1), .LOAD(LOAD), .CLK(CLK), .Q(S1));  // open: NOT_Q
  _1bit_reg u_1bit_reg_3 (.CLR(CLR), .A0(A2), .LOAD(LOAD), .CLK(CLK), .Q(S2));  // open: NOT_Q
  _1bit_reg u_1bit_reg_4 (.CLR(CLR), .A0(A3), .LOAD(LOAD), .CLK(CLK), .Q(S3));  // open: NOT_Q
  _1bit_reg u_1bit_reg_5 (.CLR(CLR), .A0(A4), .LOAD(LOAD), .CLK(CLK), .Q(S4));  // open: NOT_Q
  _1bit_reg u_1bit_reg_6 (.CLR(CLR), .A0(A5), .LOAD(LOAD), .CLK(CLK), .Q(S5));  // open: NOT_Q
  _1bit_reg u_1bit_reg_7 (.CLR(CLR), .A0(A6), .LOAD(LOAD), .CLK(CLK), .Q(S6));  // open: NOT_Q
  _1bit_reg u_1bit_reg_8 (.CLR(CLR), .A0(A7), .LOAD(LOAD), .CLK(CLK), .Q(S7));  // open: NOT_Q
endmodule

// arithmetic
module full_artim (
  input  S1,
  input  S0,
  input  CIn,
  input  A0,
  input  A1,
  input  A2,
  input  A3,
  input  A4,
  input  A5,
  input  A6,
  input  A7,
  input  B0,
  input  in_13,
  input  B1,
  input  B2,
  input  B3,
  input  B4,
  input  B5,
  input  B6,
  input  B7,
  output out_21,
  output out_22,
  output out_23,
  output out_24,
  output out_25,
  output out_26,
  output out_27,
  output out_28,
  output C_OUT
);

  adder_with_sub adder_with_sub_1 (
    .CO(CIn), .A0(A0), .B0(B0), .A1(A1), .B1(B1), .A2(A2), .B2(B2), .A3(A3), .B3(B3), .A4(A4), .B4(B4),
    .A5(A5), .B5(B5), .A6(A6), .B6(B6), .A7(A7), .B7(B7), .S0_2(out_21), .S1_2(out_22), .S2(out_23),
    .S3(out_24), .S4(out_25), .S5(out_26), .S6(out_27), .S7(out_28), .C_OUT(C_OUT), .in_20(in_13), .S1(S1),
    .S0(S0));
endmodule

module _2x1_mux (
  input  A,
  input  B,
  input  in_3,
  output out_4
);

  wire and_1_out, and_2_out, not_1_out;

  not not_1 (not_1_out, in_3);
  and and_1 (and_1_out, A, not_1_out);
  and and_2 (and_2_out, B, in_3);
  or or_1 (out_4, and_1_out, and_2_out);
endmodule

module _4x1_mux (
  input  in_1,
  input  in_2,
  input  in_3,
  input  in_4,
  input  in_5,
  input  in_6,
  output out_7
);

  wire and_1_out, and_2_out, and_3_out, and_4_out, not_1_out, not_2_out;

  not not_1 (not_1_out, in_5);
  not not_2 (not_2_out, in_6);
  and and_1 (and_1_out, in_1, not_1_out, not_2_out);
  and and_2 (and_2_out, in_2, not_1_out, in_6);
  and and_3 (and_3_out, in_3, in_5, not_2_out);
  and and_4 (and_4_out, in_4, in_5, in_6);
  or or_1 (out_7, and_1_out, and_2_out, and_3_out, and_4_out);
endmodule

module _1bit_log (
  input  A,
  input  B,
  input  S1,
  input  S0,
  output OUT_PUT
);

  wire and_1_out, not_1_out, or_1_out, xor_1_out;

  not not_1 (not_1_out, A);
  and and_1 (and_1_out, A, B);
  or or_1 (or_1_out, A, B);
  xor xor_1 (xor_1_out, A, B);
  _4x1_mux u_4x1_mux_1 (
    .in_1(and_1_out), .in_2(or_1_out), .in_3(xor_1_out), .in_4(not_1_out), .in_5(S1), .in_6(S0),
    .out_7(OUT_PUT));
endmodule

module _4bit_logic (
  input  A0,
  input  SL0,
  input  B0,
  input  SL1,
  input  A1,
  input  B1,
  input  A2,
  input  B2,
  input  A3,
  input  A3_2,
  output S0,
  output S1,
  output S2,
  output out_14
);

  _1bit_log u_1bit_log_1 (.OUT_PUT(S0), .A(A0), .B(B0), .S1(SL1), .S0(SL0));
  _1bit_log u_1bit_log_2 (.OUT_PUT(S1), .A(A1), .B(B1), .S1(SL1), .S0(SL0));
  _1bit_log u_1bit_log_3 (.OUT_PUT(S2), .A(A2), .B(B2), .S1(SL1), .S0(SL0));
  _1bit_log u_1bit_log_4 (.OUT_PUT(out_14), .A(A3), .B(A3_2), .S1(SL1), .S0(SL0));
endmodule

// logic
module _8bit_logic (
  input  A0,
  input  B0,
  input  A1,
  input  B1,
  input  A2,
  input  B2,
  input  SL1,
  input  SL0,
  input  A3,
  input  B3,
  input  A4,
  input  B4,
  input  A5,
  input  B5,
  input  A6,
  input  B6,
  input  A7,
  input  B7,
  output out_19,
  output out_20,
  output out_21,
  output out_22,
  output out_23,
  output out_24,
  output out_25,
  output out_26
);

  _4bit_logic u_4bit_logic_1 (
    .A0(A0), .B0(B0), .A1(A1), .B1(B1), .A2(A2), .B2(B2), .S0(out_19), .SL0(SL0), .SL1(SL1), .S1(out_20),
    .S2(out_21), .A3(A3), .A3_2(B3), .out_14(out_22));
  _4bit_logic u_4bit_logic_2 (
    .A0(A4), .B0(B4), .A1(A5), .B1(B5), .A2(A6), .B2(B6), .S0(out_23), .SL0(SL0), .SL1(SL1), .S1(out_24),
    .S2(out_25), .A3(A7), .A3_2(B7), .out_14(out_26));
endmodule

module _4bit_shift (
  input  in_1,
  input  _1L_0R,
  input  _0,
  input  _1,
  input  _2,
  input  _3,
  input  in_7,
  output S0,
  output S1,
  output S2,
  output S3
);

  _2x1_mux u_2x1_mux_1 (.A(_1), .B(in_1), .in_3(_1L_0R), .out_4(S0));
  _2x1_mux u_2x1_mux_2 (.A(_2), .B(_0), .in_3(_1L_0R), .out_4(S1));
  _2x1_mux u_2x1_mux_3 (.A(_3), .B(_1), .in_3(_1L_0R), .out_4(S2));
  _2x1_mux u_2x1_mux_4 (.A(in_7), .B(_2), .in_3(_1L_0R), .out_4(S3));
endmodule

// SHIFT
module _8bit_shift (
  input  in_1,
  input  _1L_0R,
  input  _0,
  input  _1,
  input  _2,
  input  _3,
  input  _4,
  input  _5,
  input  _6,
  input  _7,
  input  in_11,
  output S0,
  output S1,
  output S2,
  output S3,
  output s4,
  output S5,
  output S6,
  output S7
);

  _2x1_mux u_2x1_mux_1 (.A(_1), .B(in_1), .in_3(_1L_0R), .out_4(S0));
  _2x1_mux u_2x1_mux_2 (.A(_2), .B(_0), .in_3(_1L_0R), .out_4(S1));
  _2x1_mux u_2x1_mux_3 (.A(_3), .B(_1), .in_3(_1L_0R), .out_4(S2));
  _2x1_mux u_2x1_mux_4 (.A(_4), .B(_2), .in_3(_1L_0R), .out_4(S3));
  _2x1_mux u_2x1_mux_5 (.A(_5), .B(_3), .in_3(_1L_0R), .out_4(s4));
  _2x1_mux u_2x1_mux_6 (.A(_6), .B(_4), .in_3(_1L_0R), .out_4(S5));
  _2x1_mux u_2x1_mux_7 (.A(_7), .B(_5), .in_3(_1L_0R), .out_4(S6));
  _2x1_mux u_2x1_mux_8 (.A(in_11), .B(_6), .in_3(_1L_0R), .out_4(S7));
endmodule

module ALU (
  input  S1,
  input  S0,
  input  CO,
  input  [7:0] A,
  input  S3,
  input  S2,
  input  [7:0] B,
  input  in_8,
  input  in_9,
  input  in_10,
  input  in_11,
  input  in_12,
  output out_13,
  output out_14,
  output out_15,
  output out_16,
  output out_17,
  output out_18,
  output out_19,
  output out_20,
  output out_21
);

  wire A_out_21, A_out_22, A_out_23, A_out_24, A_out_25, A_out_26, A_out_27, A_out_28, LEFT_s0, LEFT_s1,
       LEFT_s2, LEFT_s3, LEFT_s4, LEFT_s5, LEFT_s6, LEFT_s7, n8bit_logic_1_out_19, n8bit_logic_1_out_20,
       n8bit_logic_1_out_21, n8bit_logic_1_out_22, n8bit_logic_1_out_23, n8bit_logic_1_out_24,
       n8bit_logic_1_out_25, n8bit_logic_1_out_26, not_1_out, RIGHT_s0, RIGHT_s1, RIGHT_s2, RIGHT_s3,
       RIGHT_s4, RIGHT_s5, RIGHT_s6, RIGHT_s7;

  full_artim u_A (
    .CIn(CO), .A0(A[0]), .A1(A[1]), .A2(A[2]), .A3(A[3]), .A4(A[4]), .A5(A[5]), .A6(A[6]), .A7(A[7]),
    .B0(B[0]), .B1(B[1]), .B2(B[2]), .B3(B[3]), .B4(B[4]), .B5(B[5]), .B6(B[6]), .B7(B[7]), .C_OUT(out_15),
    .out_21(A_out_21), .out_22(A_out_22), .out_23(A_out_23), .out_24(A_out_24), .out_25(A_out_25),
    .out_26(A_out_26), .out_27(A_out_27), .out_28(A_out_28), .S1(S1), .S0(S0), .in_13(in_8));
  _8bit_logic u_8bit_logic_1 (
    .A0(A[0]), .B0(B[0]), .A1(A[1]), .B1(B[1]), .A2(A[2]), .B2(B[2]), .A3(A[3]), .B3(B[3]), .A4(A[4]),
    .B4(B[4]), .A5(A[5]), .B5(B[5]), .A6(A[6]), .B6(B[6]), .A7(A[7]), .B7(B[7]), .SL1(S1), .SL0(S0),
    .out_19(n8bit_logic_1_out_19), .out_20(n8bit_logic_1_out_20), .out_21(n8bit_logic_1_out_21),
    .out_22(n8bit_logic_1_out_22), .out_23(n8bit_logic_1_out_23), .out_24(n8bit_logic_1_out_24),
    .out_25(n8bit_logic_1_out_25), .out_26(n8bit_logic_1_out_26));
  _8bit_shift RIGHT (
    ._0(A[0]), ._1(A[1]), ._2(A[2]), ._3(A[3]), ._4(A[4]), ._5(A[5]), ._6(A[6]), ._7(A[7]), .S0(RIGHT_s0),
    .S1(RIGHT_s1), .S2(RIGHT_s2), .S3(RIGHT_s3), .s4(RIGHT_s4), .S5(RIGHT_s5), .S6(RIGHT_s6), .S7(RIGHT_s7),
    .in_1(in_10), ._1L_0R(in_9), .in_11(in_11));
  not not_1 (not_1_out, in_9);
  _8bit_shift LEFT (
    ._0(A[0]), ._1(A[1]), ._2(A[2]), ._3(A[3]), ._4(A[4]), ._5(A[5]), ._6(A[6]), ._7(A[7]), .S0(LEFT_s0),
    .S1(LEFT_s1), .S2(LEFT_s2), .S3(LEFT_s3), .s4(LEFT_s4), .S5(LEFT_s5), .S6(LEFT_s6), .S7(LEFT_s7),
    .in_1(in_11), ._1L_0R(not_1_out), .in_11(in_12));
  _4x1_mux u_4x1_mux_1 (
    .in_1(A_out_21), .in_2(n8bit_logic_1_out_19), .in_3(RIGHT_s0), .in_4(LEFT_s0), .in_5(S3), .in_6(S2),
    .out_7(out_13));
  _4x1_mux u_4x1_mux_2 (
    .in_1(A_out_22), .in_2(n8bit_logic_1_out_20), .in_3(RIGHT_s1), .in_4(LEFT_s1), .in_5(S3), .in_6(S2),
    .out_7(out_14));
  _4x1_mux u_4x1_mux_3 (
    .in_1(A_out_23), .in_2(n8bit_logic_1_out_21), .in_3(RIGHT_s2), .in_4(LEFT_s2), .in_5(S3), .in_6(S2),
    .out_7(out_16));
  _4x1_mux u_4x1_mux_4 (
    .in_1(A_out_24), .in_2(n8bit_logic_1_out_22), .in_3(RIGHT_s3), .in_4(LEFT_s3), .in_5(S3), .in_6(S2),
    .out_7(out_17));
  _4x1_mux u_4x1_mux_5 (
    .in_1(A_out_25), .in_2(n8bit_logic_1_out_23), .in_3(RIGHT_s4), .in_4(LEFT_s4), .in_5(S3), .in_6(S2),
    .out_7(out_18));
  _4x1_mux u_4x1_mux_6 (
    .in_1(A_out_26), .in_2(n8bit_logic_1_out_24), .in_3(RIGHT_s5), .in_4(LEFT_s5), .in_5(S3), .in_6(S2),
    .out_7(out_19));
  _4x1_mux u_4x1_mux_7 (
    .in_1(A_out_27), .in_2(n8bit_logic_1_out_25), .in_3(RIGHT_s6), .in_4(LEFT_s6), .in_5(S3), .in_6(S2),
    .out_7(out_20));
  _4x1_mux u_4x1_mux_8 (
    .in_1(A_out_28), .in_2(n8bit_logic_1_out_26), .in_3(RIGHT_s7), .in_4(LEFT_s7), .in_5(S3), .in_6(S2),
    .out_7(out_21));
endmodule
